# Fritzing sketch Termostato (saved by Fritzing 0.9.3b)
breadboards: 1

parts:
  Componente1 = Arduino Uno (Rev3)
  U1 = TMP36 [package=to-92-kit]
  LED1 = LED - 5mm [color="Green (570nm)" package="5 mm [THT]"]
  R2 = Resistor [tolerance=±5% resistance=220 package=THT]
  LED2 = LED - 5mm [color="Red (633nm)" package="5 mm [THT]"]
  R3 = Resistor [tolerance=±5% resistance=220 package=THT]
  J1 = Piezo Speaker

nets:
  N1: Componente1.A0, U1.VOUT
  N2: Componente1.D8, J1.pin2
  GND: Componente1.GND, U1.GND, R2.Pin_0, R3.Pin_1, J1.pin1
  N3: Componente1.D6_PWM, LED1.anode
  N4: Componente1.D7, LED2.anode
  5V: Componente1.5V, U1.VCC
  N5: LED1.cathode, R2.Pin_1
  N6: LED2.cathode, R3.Pin_0

// code stored in the sketch: termostato.ino

/*


 Medida de temperatura con sensor TMP36

 Mostramos la temperatura por el monitor serie

 JA. Vacas



 Descripción



 Sensor TMP36 

 pin V del sensor conectado a 5V de Arduino

 pin central del sensor Vout a A0 de Arduino

 pin GND a GND de Arduino

 

 */



// constantes que no cambian

// se usan para establecer los pines



const int TMP36Pin = A0;     // Conectamos el pin central

const int ledVerdePin=6;     // Led que representa la refrigeracion

const int ledRojoPin=7; 		 // Led que representa la calefacción
const int alarma=8;				 // Zumbador que representa la alarma contra incendios

// variables globales que cambian

float temperatura = 0;         // variable para almacenar la temperatura medida



// Configuración

void setup() {

  Serial.begin(9600); // Configuramos la conexion con el PC

  pinMode(ledVerdePin,OUTPUT);  // Configuramos el LedVerdePin como salida
	pinMode (ledRojoPin, OUTPUT); //configuramos el led rojo como salida
	pinMode (alarma,OUTPUT); //configuramos el zumbador como salida

// No necesitamos configurar los pines analogicos

}



// Bucle que se repite

void loop() {

  int lectura = analogRead(TMP36Pin); // Valor entre 0 y 1023

  

  float voltaje = lectura * 5.0 / 1024.0; // Voltaje entre 0 y 5V



  temperatura = (voltaje - 0.5) * 100; // Temperatura en º Celsius



  Serial.print("Temperatura:");  

  Serial.print(temperatura);  // Mostramos el valor de la temperatura 

  Serial.println("C");



  if(temperatura>25) { // Si la temperatura supera los 25º 

    digitalWrite(ledVerdePin,HIGH);

    Serial.println("Activamos la refrigeracion");

  }else {

    digitalWrite(ledVerdePin,LOW);

    Serial.println("Apagamos la refrigeracion");

  }


  if(temperatura<25) { // Si la temperatura es inferior a los 25º 
    digitalWrite(ledRojoPin,HIGH);
    Serial.println("Activamos la calefacción");
  }else {
    digitalWrite(ledRojoPin,LOW);
    Serial.println("Apagamos la calefacción");
  }


  if(temperatura>40) { // Si la temperatura supera los 40º 
    digitalWrite(alarma,HIGH);
    Serial.println("Activamos la alarma contra incendios");
  }else {
    digitalWrite(alarma,LOW);
    Serial.println("No hay riesgo de incendios");
  }



}



