# Fritzing sketch Indicador_Temperaturac_LED_RGB (saved by Fritzing 0.9.3b)
breadboards: 1

parts:
  Componente1 = Arduino Uno (Rev3)
  LED1 = RGB LED (com. cathode, rgb) [package="5 mm [THT]"]
  U1 = TMP36 [package=to-92-kit]
  R1 = Resistor [tolerance=±5% resistance=220 package=THT]
  R2 = Resistor [tolerance=±5% resistance=220 package=THT]
  R3 = Resistor [tolerance=±5% resistance=220 package=THT]

nets:
  N1: Componente1.A0, U1.VOUT
  N2: Componente1.D9_PWM, R1.Pin_0
  N3: Componente1.D10_PWM/SS, R3.Pin_0
  N4: Componente1.D11_PWM/MOSI, R2.Pin_0
  5V: Componente1.5V, U1.VCC
  GND: Componente1.GND, LED1.common_cathode, U1.GND
  N5: LED1.red_anode, R1.Pin_1
  N6: LED1.green_anode, R3.Pin_1
  N7: LED1.blue_anode, R2.Pin_1

custom parts:
  RGB LED (com. cathode, rgb): A 5mm tri-color LED with red, green and blue inside.

// code stored in the sketch: Untitled4.ino



/*


Curso de Arduino

Cambio de color de una tira de LED  RGB en funcion de la temperatura

Medimos la temperatura con un TMP36



Descripcion

Mostraremos la temperatura con una escala de colores:

Frio-Azul             Calor-Rojo



Montaje



Sensor de temperatura TMP6        A0



RGB_B    10

RGB_R    9

RGB_G    11



by JAVacasM

*/



// Variables globales



const int TMP36Pin=A0;



const int ledPWM_G=11;

const int ledPWM_R=9;

const int ledPWM_B=10;





//Para escalar el color definimos una temperatura minima y una maxima

const int TEMP_MINIMA=15;

const int TEMP_MAXIMA=25;



float temperaturaC;    // Guardamos la temperatura actual



void setup() {

  Serial.begin(9600);

  analogWrite(ledPWM_G, 0); // Apagamos el verde porque no lo vamos a usar

}



void loop() {

  

  int iValorAnalogico=analogRead(TMP36Pin);  // Leemos el sensor TMP36



  float voltaje = iValorAnalogico * 5.0 / 1024.0; // voltios

  temperaturaC = (voltaje - 0.5) * 100 ;          // temperatura 



  // Enviamos la temperatura por el puerto serie

  Serial.print(iValorAnalogico);

  Serial.print(" ");

  Serial.println(temperaturaC);



  // Filtramos la temperatura fuera de rango (suelen ser problemas del sensor)

  if( (temperaturaC > TEMP_MINIMA ) && (temperaturaC < TEMP_MAXIMA)){



    // Escalamos directamente proporcial  la temperatura y el rojo

    int iBrightR=map(int(temperaturaC),TEMP_MINIMA,TEMP_MAXIMA,0,255);

    // Escalamos inversamente proporcial la temperatura y el azul

    int iBrightB=map(int(temperaturaC),TEMP_MINIMA,TEMP_MAXIMA,255,0);

  

    analogWrite(ledPWM_R, iBrightR); // establecemos el brillo de rojo

    analogWrite(ledPWM_B, iBrightB); // establecemos el brillo de azul

    

  } else {

    Serial.print("Error de lectura: ");

    Serial.println(temperaturaC);

  }

   

  delay(200);   // Esperamos un tiempo a que se estabilice el brillo

}
